// Logisim project 221020870 - Gabriel Roberto de Queiroz - Circuito.circ as structural Verilog: 8 circuits, main circuit main
module main (
  input  in_1,
  input  in_2,
  input  in_3,
  input  in_4,
  input  A,
  input  B,
  input  C,
  input  A_2,
  input  B_2,
  input  C_2,
  input  A_3,
  input  B_3,
  input  C_3,
  input  A_4,
  input  B_4,
  input  C_4,
  input  D3,
  input  D2,
  input  D1,
  input  D0,
  input  S1,
  input  S0,
  output out_23,
  output out_24,
  output out_25,
  output out_26,
  output out_27,
  output out_28,
  output out_29
);

  T_function__AND_and_OR t_function_and_and_or_1 (.A(A), .B(B), .C(C), .T(out_25));
  S_function__AND_and_OR s_function_and_and_or_1 (.A(A_3), .B(B_3), .C(C_3), .out_4(out_27));
  And_Port and_port_1 (.A(in_2), .B(in_1), .\Saída (out_23));
  Or_Port or_port_1 (.A(in_4), .B(in_3), .\Saída (out_24));
  Y_function y_function_1 (.D3(D3), .D2(D2), .D1(D1), .D0(D0), .S1(S1), .S0(S0), .out_7(out_29));
  T_function__NAND t_function_nand_1 (.A(A_2), .B(B_2), .C(C_2), .T(out_26));
  S_function__NAND s_function_nand_1 (.A(A_4), .B(B_4), .C(C_4), .out_4(out_28));

  // Notes on the sheet:
  //   Portas E e OU
  //   Portas E e OU
  //   Porta E
  //   Porta OU
  //   T = AB + AC + BC
  //   S = ^A^BC + ^AB^C + A^B^C + ABC
  //   Y = D0^S1^S0 + D1^S1S0 + D2S1^S0 + D3S1S0
  //   Portas NAND
  //   Portas NAND
endmodule

module And_Port (
  input  A,
  input  B,
  output \Saída 
);

  wire not_1_out, not_2_out, or_1_out;

  not not_1 (not_1_out, A);
  or or_1 (or_1_out, not_1_out, not_2_out);
  not not_2 (not_2_out, B);
  not not_3 (\Saída , or_1_out);
endmodule

module Or_Port (
  input  A,
  input  B,
  output \Saída 
);

  wire and_1_out, not_1_out, not_2_out;

  not not_1 (not_1_out, A);
  not not_2 (not_2_out, B);
  and and_1 (and_1_out, not_1_out, not_2_out);
  not not_3 (\Saída , and_1_out);
endmodule

module T_function__AND_and_OR (
  input  A,
  input  B,
  input  C,
  output T
);

  wire \and_port_1_saída , \and_port_2_saída , \and_port_3_saída ;

  And_Port and_port_1 (.A(A), .B(B), .\Saída (\and_port_1_saída ));
  And_Port and_port_2 (.A(A), .B(C), .\Saída (\and_port_2_saída ));
  And_Port and_port_3 (.A(B), .B(C), .\Saída (\and_port_3_saída ));
  or or_1 (T, \and_port_1_saída , \and_port_2_saída , \and_port_3_saída );
endmodule

module S_function__AND_and_OR (
  input  A,
  input  B,
  input  C,
  output out_4
);

  wire and_1_out, and_2_out, and_3_out, and_4_out, not_1_out, not_2_out, not_3_out, not_4_out, not_5_out,
       not_6_out;

  not not_1 (not_1_out, A);
  not not_2 (not_2_out, B);
  not not_3 (not_3_out, A);
  not not_4 (not_4_out, C);
  not not_5 (not_5_out, B);
  not not_6 (not_6_out, C);
  and and_1 (and_1_out, not_1_out, not_2_out, C);
  and and_2 (and_2_out, not_3_out, B, not_4_out);
  and and_3 (and_3_out, A, not_5_out, not_6_out);
  and and_4 (and_4_out, A, B, C);
  or or_1 (out_4, and_1_out, and_2_out, and_3_out, and_4_out);
endmodule

module T_function__NAND (
  input  A,
  input  B,
  input  C,
  output T
);

  wire nand_1_out, nand_2_out, nand_3_out;

  nand nand_1 (nand_1_out, A, B);
  nand nand_2 (nand_2_out, A, C);
  nand nand_3 (nand_3_out, B, C);
  nand nand_4 (T, nand_1_out, nand_2_out, nand_3_out);
endmodule

module S_function__NAND (
  input  A,
  input  B,
  input  C,
  output out_4
);

  wire nand_1_out, nand_2_out, nand_3_out, nand_4_out;

  nand nand_1 (nand_1_out, ~A, ~B, C);  // NAND_Gate
  nand nand_2 (nand_2_out, ~A, B, ~C);  // NAND_Gate
  nand nand_3 (nand_3_out, A, ~B, ~C);  // NAND_Gate
  nand nand_4 (nand_4_out, A, B, C);
  nand nand_5 (out_4, nand_1_out, nand_2_out, nand_3_out, nand_4_out);
endmodule

module Y_function (
  input  D3,
  input  D2,
  input  D1,
  input  D0,
  input  S1,
  input  S0,
  output out_7
);

  wire nand_1_out, nand_2_out, nand_3_out, nand_4_out;

  nand nand_1 (nand_1_out, D0, ~S1, ~S0);  // NAND_Gate
  nand nand_2 (nand_2_out, D1, ~S1, S0);  // NAND_Gate
  nand nand_3 (nand_3_out, D2, S1, ~S0);  // NAND_Gate
  nand nand_4 (nand_4_out, D3, S1, S0);
  nand nand_5 (out_7, nand_1_out, nand_2_out, nand_3_out, nand_4_out);
endmodule
