// Logisim project abc_to_xy.circ as structural Verilog: 1 circuit, main circuit main
module main (
  input  [2:0] Entrada,
  output [1:0] XY
);

  wire not_1_out;

  // NoConnect on Entrada[0]
  Multiplexer #(.select(2)) multiplexer_1 (
    .in0(1'b1), .in1(not_1_out), .in2(1'b0), .in3(Entrada[0]), .out(XY[0]), .sel(Entrada[2:1]));
  not not_1 (not_1_out, Entrada[0]);
  Multiplexer #(.select(2)) multiplexer_2 (
    .in0(1'b0), .in1(Entrada[0]), .in2(not_1_out), .in3(1'b1), .out(XY[1]), .sel(Entrada[2:1]));

  // Other names for the same wires on the sheet: AB[1:0] = Entrada[2:1]; ABC[2:0] = Entrada; B = Entrada[1];
  //   A = Entrada[2]; C = Entrada[0]
endmodule
