// Logisim project abcdefg_to_s.circ as structural Verilog: 1 circuit, main circuit main
module main (
  input  A,
  input  B,
  input  C,
  input  D,
  input  E,
  input  F,
  input  G,
  output [6:0] Entrada,
  output Saida
);

  wire ABCD, AnBCD, AnBCnD, AnBnCD, decoder_1_out1, decoder_1_out2, decoder_1_out3, decoder_1_out4,
       decoder_1_out5, decoder_1_out6, decoder_1_out8, decoder_1_out12, decoder_1_out13, decoder_1_out14,
       nABCD, nAnBnCnD, or_1_out, or_2_out, or_3_out;

  Decoder #(.select(4)) decoder_1 (
    .out0(nAnBnCnD), .out1(decoder_1_out1), .out2(decoder_1_out2), .out3(decoder_1_out3),
    .out4(decoder_1_out4), .out5(decoder_1_out5), .out6(decoder_1_out6), .out7(nABCD), .out8(decoder_1_out8),
    .out9(AnBnCD), .out10(AnBCD), .out11(AnBCnD), .out12(decoder_1_out12), .out13(decoder_1_out13),
    .out14(decoder_1_out14), .out15(ABCD), .sel({A, B, C, D}), .en(1'b1));
  // NoConnect on decoder_1_out1
  // NoConnect on decoder_1_out2
  // NoConnect on decoder_1_out3
  // NoConnect on decoder_1_out4
  // NoConnect on decoder_1_out5
  // NoConnect on decoder_1_out6
  // NoConnect on decoder_1_out8
  or or_1 (or_1_out, ABCD, nAnBnCnD);
  Multiplexer #(.select(3)) multiplexer_1 (
    .in0(ABCD), .in1(or_1_out), .in2(nABCD), .in3(1'b1), .in4(or_2_out), .in5(1'b0), .in6(or_3_out),
    .in7(1'b1), .out(Saida), .sel({E, F, G}));
  // NoConnect on decoder_1_out12
  // NoConnect on decoder_1_out13
  // NoConnect on decoder_1_out14
  or or_2 (or_2_out, ABCD, AnBnCD);
  or or_3 (or_3_out, AnBCnD, AnBCD);

  assign Entrada = {A, B, C, D, E, F, G};
endmodule
