// Logisim project words_adder_topmodule.circ as structural Verilog: 4 circuits, main circuit main
module main (
);

  wire [3:0] A, B;
  wire [4:0] dut_1_s, gm_1_s;

  gm gm_1 (.A(A), .B(B), .S(gm_1_s));
  dut dut_1 (.B(B), .A(A), .S(dut_1_s));
  testbench testbench_1 (.GM_OUT(gm_1_s), .DUT_OUT(dut_1_s), .A(A), .B(B));
endmodule

module gm (
  input  [3:0] A,
  input  [3:0] B,
  output [4:0] S
);

  Adder #(.width(4)) adder_1 (.a(A), .b(B), .out(S[3:0]), .cin(1'b0), .cout(S[4]));
endmodule

module dut (
  input  [3:0] B,
  input  [3:0] A,
  output [4:0] S
);

  wire adder_1_cout, adder_2_cout, adder_3_cout;

  Adder #(.width(1)) adder_1 (.a(A[0]), .b(B[0]), .out(S[0]), .cin(1'b0), .cout(adder_1_cout));
  Adder #(.width(1)) adder_2 (.a(A[1]), .b(B[1]), .out(S[1]), .cin(adder_1_cout), .cout(adder_2_cout));
  Adder #(.width(1)) adder_3 (.a(A[2]), .b(B[2]), .out(S[2]), .cin(adder_2_cout), .cout(adder_3_cout));
  Adder #(.width(1)) adder_4 (.a(A[3]), .b(B[3]), .out(S[3]), .cin(adder_3_cout), .cout(S[4]));
endmodule

module testbench (
  input  [4:0] GM_OUT,
  input  [4:0] DUT_OUT,
  output [3:0] A,
  output [3:0] B
);
endmodule
