// Logisim project 1 - Full_adder.circ as structural Verilog: 1 circuit, main circuit Validacao
module Validacao (
  input  [1:0] A,
  input  [1:0] B,
  output [2:0] out_3
);

  wire adder_1_cout;

  Adder #(.width(1)) adder_1 (.a(A[0]), .b(B[0]), .out(out_3[0]), .cin(1'b0), .cout(adder_1_cout));
  Adder #(.width(1)) adder_2 (.a(A[1]), .b(B[1]), .out(out_3[1]), .cin(adder_1_cout), .cout(out_3[2]));
endmodule
